# Fritzing sketch HomeSprinkler (saved by Fritzing 0.9.3b)
breadboards: 1

parts:
  WeMos_D1_Mini1 = WeMos D1 Mini
  Часть1 = Soil Moisture Sensor
  Q1 = Basic FET N-Channel [package="TO220 [THT]"]
  M1 = RioRand LM2596
  R1 = Resistor [tolerance=±5% resistance=470 package=THT]
  M2 = DC Motor
  V1 = DC Power [voltage=12V]

nets:
  3V3: WeMos_D1_Mini1.3V3, Часть1.VCC, M1.Pin_3
  N1: WeMos_D1_Mini1.A0, Часть1.SIG
  N2: WeMos_D1_Mini1.D5, R1.Pin_1
  GND: WeMos_D1_Mini1.G, Часть1.GND, Q1.source, M1.Pin_2, M1.Pin_4, V1.V-
  N3: Q1.gate, R1.Pin_0
  N4: Q1.drain, M2.pin_2
  N5: M1.Pin_1, M2.pin_1, V1.V+
